# Fritzing sketch 170713_WiringDiagram (saved by Fritzing 0.9.3b)
perfboards: 1

parts:
  Part1 = Arduino Uno (Rev3)
  9V_Voltage_Regulator = Voltage Regulator [part_number="\nL78S09CV"]
  3S_Lipo_Battery1 = 3 Cell 1300 mAh Lipo Battery
  R1 = Resistor [tolerance=±5% resistance=220 package="0402 [SMD]"]
  Part2 = Adafruit Breadboard-Friendly NeoPixel [part_number="Adafruit #1312"]
  R2 = Resistor [tolerance=±5% resistance=220 package="0402 [SMD]"]
  D3 = Diode [package=diode-1n4001]
  R3 = Resistor [tolerance=±5% resistance=220 package="0402 [SMD]"]
  Q1 = Basic FET N-Channel [package="DPak [SMD]"]
  Q2 = Basic FET N-Channel [package="DPak [SMD]"]
  Q3 = Basic FET N-Channel [package="DPak [SMD]"]
  M1 = DC Motor
  M2 = DC Motor
  M3 = DC Motor
  D2 = Diode [package=diode-1n4001]
  D4 = Diode [package=diode-1n4001]
  R6 = Resistor [tolerance=±5% resistance=220 package="0402 [SMD]"]
  R4 = Resistor [tolerance=±5% resistance=220 package="0402 [SMD]"]
  R5 = Resistor [tolerance=±5% resistance=220 package="0402 [SMD]"]
  S1 = Reed switch [package=THT]

nets:
  N1: Part1.D9_PWM, R3.Pin_1
  N2: Part1.D10_PWM/SS, R2.Pin_1
  N3: Part1.D11_PWM/MOSI, R1.Pin_1
  GND: Part1.GND, 9V_Voltage_Regulator.IN, 3S_Lipo_Battery1.-, Part2.GND, S1.pin_1
  N4: Part1.D1/TX, Part2.IN
  N5: Part1.D7, S1.pin_2
  5V: Part1.5V, Part2.VDD
  N6: Part1.VIN, 9V_Voltage_Regulator.OUT
  N7: 9V_Voltage_Regulator.ADJ, 3S_Lipo_Battery1.+, D3.C, M1.pin_1, M2.pin_1, M3.pin_1, D2.C, D4.C
  N8: R1.Pin_0, Q1.Gate, R4.Pin_1
  N9: R2.Pin_0, Q2.Gate, R5.Pin_1
  N10: D3.A, Q3.drain, M3.pin_2
  N11: R3.Pin_0, Q3.Gate, R6.Pin_1
  N12: Q1.drain, M1.pin_2, D4.A
  N13: Q1.source, R4.Pin_0
  N14: Q2.drain, M2.pin_2, D2.A
  N15: Q2.source, R5.Pin_0
  N16: Q3.source, R6.Pin_0

custom parts:
  Voltage Regulator: Voltage Regulator linear voltage regulators
  3 Cell 1300 mAh Lipo Battery: Turnigy nano-tech 1300mAh 3S 45~90C Lipo Pack
  Adafruit Breadboard-Friendly NeoPixel: This is the easiest way possible to add small, bright RGB pixels to your project. We took the same technology from our Flora NeoPixels and made them breadboard friendly, with two rows of 3 x 0.1" spaced header on each side for easy soldering, chaining and breadboarding. These ultra-bright LEDs have a constant-current driver cooked right into the LED package! The pixels are chainable - so you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
