# Fritzing sketch 170719_MotorDriver (saved by Fritzing 0.9.3b)
perfboards: 1

parts:
  R7 = Resistor [tolerance=±5% resistance=220 package="0402 [SMD]"]
  R8 = Resistor [tolerance=±5% resistance=220 package="0402 [SMD]"]
  R9 = Resistor [tolerance=±5% resistance=220 package="0402 [SMD]"]
  R10 = Resistor [tolerance=±5% resistance=220 package="0402 [SMD]"]
  R11 = Resistor [tolerance=±5% resistance=220 package="0402 [SMD]"]
  D5 = Diode [package=diode-1n4001]
  Q4 = Basic FET N-Channel [package="DPak [SMD]"]
  Q5 = Basic FET N-Channel [package="DPak [SMD]"]
  Q6 = Basic FET N-Channel [package="DPak [SMD]"]
  Motor_3 = DC Motor
  D6 = Diode [package=diode-1n4001]
  D7 = Diode [package=diode-1n4001]
  R12 = Resistor [tolerance=±5% resistance=220 package="0402 [SMD]"]
  Motor_2 = DC Motor
  Motor_1 = DC Motor

nets:
  N1: R7.Pin_0, Q6.source
  N2: R7.Pin_1, R11.Pin_0, Q6.Gate
  N3: R8.Pin_0, Q5.source
  N4: R8.Pin_1, R10.Pin_0, Q5.Gate
  N5: R9.Pin_0, Q4.Gate, R12.Pin_1
  N6: D5.A, Q5.drain, Motor_3.pin_2
  N7: D5.C, Motor_3.pin_1, D6.C, D7.C, Motor_2.pin_1, Motor_1.pin_1
  N8: Q4.drain, D7.A, Motor_1.pin_2
  N9: Q4.source, R12.Pin_0
  N10: Q6.drain, D6.A, Motor_2.pin_2

notes:
  Sig2
  Sig1
  Sig3
  12V
  GND
